# Fritzing sketch paparazzi (saved by Fritzing 0.9.3b)
breadboards: 1

parts:
  Part1 = Adafruit Pi Cobbler Plus [part_number="Adafruit #2029"]
  LED1 = LED - 5mm [color="Red (633nm)" package="5 mm [THT]"]
  LED2 = LED - 5mm [color="Green (555nm)" package="5 mm [THT]"]
  LED3 = LED - 5mm [color="Blue (505nm)" package="5 mm [THT]"]
  S1 = Pushbutton [package="[SMD]"]
  C1 = Electrolytic Capacitor [capacitance=1µF package="100 mil [THT, electrolytic]"]
  R1 = PHOTOCELL [package=photocell]
  hc-sr1 = hc-sr04
  R2 = Resistor [tolerance=±5% resistance=1k package="2512 [SMD]"]
  R3 = Resistor [tolerance=±5% resistance=1k package="2512 [SMD]"]
  R4 = Resistor [tolerance=±5% resistance=1k package="2512 [SMD]"]
  R5 = Resistor [tolerance=±5% resistance=560 package="2512 [SMD]"]
  R6 = Resistor [tolerance=±5% resistance=560 package="2512 [SMD]"]
  R7 = Resistor [tolerance=±5% resistance=560 package="2512 [SMD]"]
  R8 = Resistor [tolerance=±5% resistance=10k package="2512 [SMD]"]

nets:
  N1: Part1.+3.3V, R1.P$1
  GND: Part1.GND, S1.Pin_3, S1.Pin_4, C1.-, hc-sr1.GND, R4.Pin_0, R5.Pin_1, R6.Pin_1, R7.Pin_1, R8.Pin_1
  N2: Part1.GPIO5, LED2.anode
  N3: Part1.GPIO6, LED1.anode
  N4: Part1.GPIO13, LED3.anode
  +5V: Part1.+5V, hc-sr1.VCC
  N5: Part1.GPIO18, C1.+, R1.P$2
  N6: Part1.GPIO23, S1.Pin_1, S1.Pin_2, R8.Pin_0
  N7: Part1.GPIO20, hc-sr1.Trig
  N8: Part1.GPIO21, R2.Pin_0, R3.Pin_1
  N9: LED1.cathode, R6.Pin_0
  N10: LED2.cathode, R7.Pin_0
  N11: LED3.cathode, R5.Pin_0
  N12: hc-sr1.Echo, R2.Pin_1
  N13: R3.Pin_0, R4.Pin_1

custom parts:
  Adafruit Pi Cobbler Plus: The Raspberry Pi B+/Pi 2/ Pi 3 has landed on the Maker World like a 40-GPIO pinned, quad-USB ported, credit card sized bomb of DIY joy. And while you can use most of our great Model B accessories by hooking up our downgrade cable, its probably a good time to upgrade your set up and accessorize using all of the Model B+'s / Pi 2's / Pi 3's 40 pins. That's why we now carry the Adafruit Assembled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
